// Logisim project Hradek-Chloe-proj1.circ as structural Verilog: 15 circuits, main circuit Arch
module Arch (
  input  [7:0] A,
  input  [7:0] B,
  input  [2:0] opcode,
  output [7:0] O
);

  ALU alu_1 (.A(A), .B(B), .opcode(opcode), .O(O));  // open: cout
endmodule

module ALU (
  input  [7:0] A,
  input  [7:0] B,
  input  [2:0] opcode,
  output [7:0] O,
  output cout
);

  wire [7:0] add_1_sumresult, andevaulator_1_cout, equalevaulator_1_result, logicalshifter_1_shiftresult,
       multiply_1_productresult, orevaulator_1_cout, subtract_1_differenceresult, xorevaulator_1_cout;

  EqualEvaulator equalevaulator_1 (.B(B), .Result(equalevaulator_1_result));
  XorEvaulator xorevaulator_1 (.A(A), .B(B), .Cout(xorevaulator_1_cout));
  ANDEvaulator andevaulator_1 (.A(A), .B(B), .Cout(andevaulator_1_cout));
  OREvaulator orevaulator_1 (.A(A), .B(B), .Cout(orevaulator_1_cout));
  Add add_1 (.A(A), .B(B), .SumResult(add_1_sumresult));
  Subtract subtract_1 (.A(A), .B(B), .DifferenceResult(subtract_1_differenceresult));
  LogicalShifter logicalshifter_1 (.B(B), .ShiftResult(logicalshifter_1_shiftresult));
  Multiply multiply_1 (.B(A), .A(B), .ProductResult(multiply_1_productresult));
  Multiplexer #(.select(3), .width(8)) multiplexer_1 (
    .in0(equalevaulator_1_result), .in1(xorevaulator_1_cout), .in2(andevaulator_1_cout),
    .in3(orevaulator_1_cout), .in4(add_1_sumresult), .in5(subtract_1_differenceresult),
    .in6(logicalshifter_1_shiftresult), .in7(multiply_1_productresult), .out(O), .sel(opcode));

  // Notes on the sheet:
  //   INPUTS
  //   O = B
  //   A XOR B
  //   A AND B
  //   A OR B
  //   A + B
  //   A - B
  //   Right Logical Shift
  //   A x B
  //   OUTPUT
endmodule

module HalfAdder (
  input  A,
  input  B,
  output Sum,
  output Carry
);

  and and_1 (Carry, A, B);
  xor xor_1 (Sum, A, B);

  // Notes on the sheet:
  //   HalfAdder in 1-bit
endmodule

module FullAdder (
  input  A,
  input  B,
  input  Cin,
  output sum,
  output carry
);

  wire halfadder_1_carry, halfadder_1_sum, halfadder_2_carry;

  HalfAdder halfadder_1 (.A(A), .B(B), .Sum(halfadder_1_sum), .Carry(halfadder_1_carry));
  HalfAdder halfadder_2 (.A(Cin), .B(halfadder_1_sum), .Sum(sum), .Carry(halfadder_2_carry));
  or or_1 (carry, halfadder_2_carry, halfadder_1_carry);

  // Notes on the sheet:
  //   Full Adder in 1-bit
endmodule

module Subtract (
  input  [7:0] A,
  input  [7:0] B,
  output [7:0] DifferenceResult
);

  wire fullsubtractor_1_bout, fullsubtractor_2_bout, fullsubtractor_3_bout, fullsubtractor_4_bout,
       fullsubtractor_5_bout, fullsubtractor_6_bout, fullsubtractor_7_bout;

  FullSubtractor fullsubtractor_1 (
    .A(A[0]), .B(B[0]), .Bin(1'b0), .Difference(DifferenceResult[0]), .Bout(fullsubtractor_1_bout));
  FullSubtractor fullsubtractor_2 (
    .A(A[1]), .B(B[1]), .Bin(fullsubtractor_1_bout), .Difference(DifferenceResult[1]),
    .Bout(fullsubtractor_2_bout));
  FullSubtractor fullsubtractor_3 (
    .A(A[2]), .B(B[2]), .Bin(fullsubtractor_2_bout), .Difference(DifferenceResult[2]),
    .Bout(fullsubtractor_3_bout));
  FullSubtractor fullsubtractor_4 (
    .A(A[3]), .B(B[3]), .Bin(fullsubtractor_3_bout), .Difference(DifferenceResult[3]),
    .Bout(fullsubtractor_4_bout));
  FullSubtractor fullsubtractor_5 (
    .A(A[4]), .B(B[4]), .Bin(fullsubtractor_4_bout), .Difference(DifferenceResult[4]),
    .Bout(fullsubtractor_5_bout));
  FullSubtractor fullsubtractor_6 (
    .A(A[5]), .B(B[5]), .Bin(fullsubtractor_5_bout), .Difference(DifferenceResult[5]),
    .Bout(fullsubtractor_6_bout));
  FullSubtractor fullsubtractor_7 (
    .A(A[6]), .B(B[6]), .Bin(fullsubtractor_6_bout), .Difference(DifferenceResult[6]),
    .Bout(fullsubtractor_7_bout));
  FullSubtractor fullsubtractor_8 (
    .A(A[7]), .B(B[7]), .Bin(fullsubtractor_7_bout), .Difference(DifferenceResult[7]));  // open: Bout

  // Notes on the sheet:
  //   Evaluate A - B
endmodule

module Multiply (
  input  [7:0] B,
  input  [7:0] A,
  output [7:0] ProductResult
);

  wire fullmultiply_1_p0, fullmultiply_1_p1, fullmultiply_1_p2, fullmultiply_1_p3, fullmultiply_2_p4,
       fullmultiply_2_p5, fullmultiply_2_p6, fullmultiply_2_p7;

  or or_1 (ProductResult[7], fullmultiply_1_p3, fullmultiply_2_p7);
  or or_2 (ProductResult[6], fullmultiply_1_p2, fullmultiply_2_p6);
  FullMultiply fullmultiply_1 (
    .a3(A[7]), .a2(A[6]), .a1(A[5]), .a0(A[4]), .b3(B[7]), .b2(B[6]), .b1(B[5]), .b0(B[4]),
    .p0(fullmultiply_1_p0), .p1(fullmultiply_1_p1), .p2(fullmultiply_1_p2), .p3(fullmultiply_1_p3));  // open: p7, p6, p5, p4
  or or_3 (ProductResult[5], fullmultiply_1_p1, fullmultiply_2_p5);
  or or_4 (ProductResult[4], fullmultiply_1_p0, fullmultiply_2_p4);
  FullMultiply fullmultiply_2 (
    .a3(A[3]), .a2(A[2]), .a1(A[1]), .a0(A[0]), .b3(B[3]), .b2(B[2]), .b1(B[1]), .b0(B[0]),
    .p0(ProductResult[0]), .p1(ProductResult[1]), .p2(ProductResult[2]), .p7(fullmultiply_2_p7),
    .p6(fullmultiply_2_p6), .p5(fullmultiply_2_p5), .p3(ProductResult[3]), .p4(fullmultiply_2_p4));

  // Notes on the sheet:
  //   Evaualte A x B
  //   Only Put 4 bits each to avoid overflow
  //   Suppose the product does not overflow
endmodule

module EqualEvaulator (
  input  [7:0] B,
  output [7:0] Result
);


  assign Result = B;

  // Notes on the sheet:
  //   Set B equal to the Output
endmodule

module ANDEvaulator (
  input  [7:0] A,
  input  [7:0] B,
  output [7:0] Cout
);

  and and_1 (Cout[0], A[0], B[0]);
  and and_2 (Cout[1], A[1], B[1]);
  and and_3 (Cout[2], A[2], B[2]);
  and and_4 (Cout[3], A[3], B[3]);
  and and_5 (Cout[4], A[4], B[4]);
  and and_6 (Cout[5], A[5], B[5]);
  and and_7 (Cout[6], A[6], B[6]);
  and and_8 (Cout[7], A[7], B[7]);

  // Notes on the sheet:
  //   Evaualte AND
endmodule

module OREvaulator (
  input  [7:0] A,
  input  [7:0] B,
  output [7:0] Cout
);

  or or_1 (Cout[0], A[0], B[0]);
  or or_2 (Cout[1], A[1], B[1]);
  or or_3 (Cout[2], A[2], B[2]);
  or or_4 (Cout[3], A[3], B[3]);
  or or_5 (Cout[4], A[4], B[4]);
  or or_6 (Cout[5], A[5], B[5]);
  or or_7 (Cout[6], A[6], B[6]);
  or or_8 (Cout[7], A[7], B[7]);

  // Notes on the sheet:
  //   Evaluate OR
endmodule

module XorEvaulator (
  input  [7:0] A,
  input  [7:0] B,
  output [7:0] Cout
);

  xor xor_1 (Cout[0], A[0], B[0]);
  xor xor_2 (Cout[1], A[1], B[1]);
  xor xor_3 (Cout[2], A[2], B[2]);
  xor xor_4 (Cout[3], A[3], B[3]);
  xor xor_5 (Cout[4], A[4], B[4]);
  xor xor_6 (Cout[5], A[5], B[5]);
  xor xor_7 (Cout[6], A[6], B[6]);
  xor xor_8 (Cout[7], A[7], B[7]);

  // Notes on the sheet:
  //   Evaluate XOR
endmodule

module LogicalShifter (
  input  [7:0] B,
  output [7:0] ShiftResult
);

  wire and_1_out, and_3_out, and_4_out, and_5_out, and_6_out, and_7_out, and_8_out, and_9_out, and_10_out,
       and_11_out, and_12_out, and_14_out, not_1_out;

  not not_1 (not_1_out, 1'b0);
  and and_1 (and_1_out, B[7], not_1_out);
  and and_2 (ShiftResult[7], 1'b0, B[6]);
  and and_3 (and_3_out, B[6], not_1_out);
  or or_1 (ShiftResult[6], and_1_out, and_4_out);
  and and_4 (and_4_out, 1'b0, B[5]);
  or or_2 (ShiftResult[5], and_3_out, and_6_out);
  and and_5 (and_5_out, B[5], not_1_out);
  and and_6 (and_6_out, 1'b0, B[4]);
  or or_3 (ShiftResult[4], and_5_out, and_8_out);
  and and_7 (and_7_out, B[4], not_1_out);
  or or_4 (ShiftResult[3], and_7_out, and_9_out);
  and and_8 (and_8_out, 1'b0, B[3]);
  or or_5 (ShiftResult[2], and_10_out, and_12_out);
  and and_9 (and_9_out, B[3], not_1_out);
  and and_10 (and_10_out, 1'b0, B[2]);
  or or_6 (ShiftResult[1], and_11_out, and_14_out);
  and and_11 (and_11_out, B[2], not_1_out);
  and and_12 (and_12_out, 1'b0, B[1]);
  and and_13 (ShiftResult[0], B[1], not_1_out);
  and and_14 (and_14_out, 1'b0, B[0]);

  // Notes on the sheet:
  //   Logically Shift Right
endmodule

module Add (
  input  [7:0] A,
  input  [7:0] B,
  output [7:0] SumResult
);

  wire fulladder_1_carry, fulladder_2_carry, fulladder_3_carry, fulladder_4_carry, fulladder_5_carry,
       fulladder_6_carry, fulladder_7_carry;

  FullAdder fulladder_1 (.A(A[0]), .B(B[0]), .Cin(1'b0), .sum(SumResult[0]), .carry(fulladder_1_carry));
  FullAdder fulladder_2 (.A(A[1]), .B(B[1]), .Cin(fulladder_1_carry), .sum(SumResult[1]), .carry(fulladder_2_carry));
  FullAdder fulladder_3 (.A(A[2]), .B(B[2]), .Cin(fulladder_2_carry), .sum(SumResult[2]), .carry(fulladder_3_carry));
  FullAdder fulladder_4 (.A(A[3]), .B(B[3]), .Cin(fulladder_3_carry), .sum(SumResult[3]), .carry(fulladder_4_carry));
  FullAdder fulladder_5 (.A(A[4]), .B(B[4]), .Cin(fulladder_4_carry), .sum(SumResult[4]), .carry(fulladder_5_carry));
  FullAdder fulladder_6 (.A(A[5]), .B(B[5]), .Cin(fulladder_5_carry), .sum(SumResult[5]), .carry(fulladder_6_carry));
  FullAdder fulladder_7 (.A(A[6]), .B(B[6]), .Cin(fulladder_6_carry), .sum(SumResult[6]), .carry(fulladder_7_carry));
  FullAdder fulladder_8 (.A(A[7]), .B(B[7]), .Cin(fulladder_7_carry), .sum(SumResult[7]));  // open: carry

  // Notes on the sheet:
  //   Evauate A + B
endmodule

module FullMultiply (
  input  a3,
  input  a2,
  input  a1,
  input  a0,
  input  b3,
  input  b2,
  input  b1,
  input  b0,
  output p0,
  output p1,
  output p2,
  output p7,
  output p6,
  output p5,
  output p3,
  output p4
);

  wire and_1_out, and_2_out, and_3_out, and_4_out, and_5_out, and_6_out, and_7_out, and_8_out, and_9_out,
       and_10_out, and_11_out, and_12_out, and_13_out, and_14_out, and_15_out, fulladder4bit_2_cout,
       fulladder4bit_2_s1, fulladder4bit_2_s2, fulladder4bit_2_s3, fulladder4bit_3_cout, fulladder4bit_3_s1,
       fulladder4bit_3_s2, fulladder4bit_3_s3;

  and and_1 (and_1_out, a3, b3);
  and and_2 (and_2_out, a3, b2);
  and and_3 (and_3_out, a3, b1);
  and and_4 (and_4_out, a3, b0);
  FullAdder4Bit fulladder4bit_1 (
    .A0(and_4_out), .A1(and_3_out), .B1(fulladder4bit_2_s2), .B2(fulladder4bit_2_s3),
    .B0(fulladder4bit_2_s1), .A2(and_2_out), .A3(and_1_out), .B3(fulladder4bit_2_cout), .s3(p6), .s2(p5),
    .s0(p3), .s1(p4), .cout(p7));
  and and_5 (and_5_out, a2, b3);
  and and_6 (and_6_out, a2, b2);
  and and_7 (and_7_out, a2, b0);
  and and_8 (and_8_out, a2, b1);
  and and_9 (and_9_out, a1, b3);
  FullAdder4Bit fulladder4bit_2 (
    .A0(and_7_out), .A1(and_8_out), .B1(fulladder4bit_3_s2), .B2(fulladder4bit_3_s3),
    .B0(fulladder4bit_3_s1), .A2(and_6_out), .A3(and_5_out), .B3(fulladder4bit_3_cout),
    .s3(fulladder4bit_2_s3), .s2(fulladder4bit_2_s2), .s0(p2), .s1(fulladder4bit_2_s1),
    .cout(fulladder4bit_2_cout));
  and and_10 (and_10_out, a1, b2);
  and and_11 (and_11_out, a1, b1);
  and and_12 (and_12_out, a1, b0);
  and and_13 (and_13_out, a0, b3);
  and and_14 (and_14_out, a0, b2);
  FullAdder4Bit fulladder4bit_3 (
    .A0(and_12_out), .A1(and_11_out), .B1(and_14_out), .B2(and_13_out), .B0(and_15_out), .A2(and_10_out),
    .A3(and_9_out), .B3(1'b0), .s3(fulladder4bit_3_s3), .s2(fulladder4bit_3_s2), .s0(p1),
    .s1(fulladder4bit_3_s1), .cout(fulladder4bit_3_cout));
  and and_15 (and_15_out, a0, b1);
  and and_16 (p0, a0, b0);
endmodule

module FullSubtractor (
  input  A,
  input  B,
  input  Bin,
  output Difference,
  output Bout
);

  wire and_1_out, and_2_out, not_1_out, not_2_out, xor_1_out;

  xor xor_1 (xor_1_out, B, Bin);
  not not_1 (not_1_out, B);
  and and_1 (and_1_out, not_1_out, Bin);
  xor xor_2 (Difference, A, xor_1_out);
  not not_2 (not_2_out, xor_1_out);
  and and_2 (and_2_out, not_2_out, A);
  or or_1 (Bout, and_2_out, and_1_out);

  // Notes on the sheet:
  //   Full Subtractor in 1-bit
endmodule

module FullAdder4Bit (
  input  A0,
  input  A1,
  input  B1,
  input  B2,
  input  B0,
  input  A2,
  input  A3,
  input  B3,
  output s3,
  output s2,
  output s0,
  output s1,
  output cout
);

  wire fulladder_1_carry, fulladder_2_carry, fulladder_3_carry, xor_1_out, xor_2_out, xor_3_out, xor_4_out;

  xor xor_1 (xor_1_out, B0, 1'b0);
  xor xor_2 (xor_2_out, 1'b0, B1);
  FullAdder fulladder_1 (.A(A0), .B(xor_1_out), .Cin(1'b0), .sum(s0), .carry(fulladder_1_carry));
  xor xor_3 (xor_3_out, 1'b0, B2);
  FullAdder fulladder_2 (.A(A1), .B(xor_2_out), .Cin(fulladder_1_carry), .sum(s1), .carry(fulladder_2_carry));
  FullAdder fulladder_3 (.A(A2), .B(xor_3_out), .Cin(fulladder_2_carry), .sum(s2), .carry(fulladder_3_carry));
  xor xor_4 (xor_4_out, 1'b0, B3);
  FullAdder fulladder_4 (.A(A3), .B(xor_4_out), .Cin(fulladder_3_carry), .sum(s3), .carry(cout));

  // Notes on the sheet:
  //   Full Adder in 4-bit
endmodule
