// Logisim project prj1.circ as structural Verilog: 5 circuits, main circuit ALU
module Arch (
  input  [7:0] A,
  input  [7:0] B,
  input  [2:0] opcode,
  output [7:0] O
);

  ALU alu_1 (.A(A), .B(B), .opcode(opcode), .O(O));  // open: cout
endmodule

module ALU (
  input  [7:0] A,
  input  [7:0] B,
  input  [2:0] opcode,
  output [7:0] O,
  output cout
);

  wire [7:0] eightbitadder_1_sum;

  EightBitAdder eightbitadder_1 (.A(A), .B(B), .Sum(eightbitadder_1_sum));  // open: FirstCarry, CarryOut
  Multiplexer #(.select(3), .width(8)) multiplexer_1 (
    .in7(eightbitadder_1_sum), .out(O), .sel(opcode));  // open: in0, in1, in2, in3, in4, in5, in6
endmodule

module HalfAdder (
  input  A,
  input  B,
  output Sum,
  output Carry
);

  xor xor_1 (Sum, A, B);
  and and_1 (Carry, A, B);
endmodule

module FullAdder (
  input  A,
  input  B,
  input  C,
  output Sum,
  output Carry
);

  wire halfadder_1_carry, halfadder_1_sum, halfadder_2_carry;

  HalfAdder halfadder_1 (.A(B), .B(C), .Sum(halfadder_1_sum), .Carry(halfadder_1_carry));
  HalfAdder halfadder_2 (.A(A), .B(halfadder_1_sum), .Sum(Sum), .Carry(halfadder_2_carry));
  or or_1 (Carry, halfadder_2_carry, halfadder_1_carry);
endmodule

module EightBitAdder (
  input  FirstCarry,
  input  [7:0] A,
  input  [7:0] B,
  output [7:0] Sum,
  output CarryOut
);

  wire fulladder_1_carry, fulladder_2_carry, fulladder_3_carry, fulladder_4_carry, fulladder_5_carry,
       fulladder_6_carry, fulladder_7_carry;

  FullAdder fulladder_1 (.A(FirstCarry), .B(A[0]), .C(B[0]), .Sum(Sum[0]), .Carry(fulladder_1_carry));
  FullAdder fulladder_2 (.A(fulladder_7_carry), .B(A[4]), .C(B[4]), .Sum(Sum[4]), .Carry(fulladder_2_carry));
  FullAdder fulladder_3 (.A(fulladder_1_carry), .B(A[1]), .C(B[1]), .Sum(Sum[1]), .Carry(fulladder_3_carry));
  FullAdder fulladder_4 (.A(fulladder_2_carry), .B(A[5]), .C(B[5]), .Sum(Sum[5]), .Carry(fulladder_4_carry));
  FullAdder fulladder_5 (.A(fulladder_3_carry), .B(A[2]), .C(B[2]), .Sum(Sum[2]), .Carry(fulladder_5_carry));
  FullAdder fulladder_6 (.A(fulladder_4_carry), .B(A[6]), .C(B[6]), .Sum(Sum[6]), .Carry(fulladder_6_carry));
  FullAdder fulladder_7 (.A(fulladder_5_carry), .B(A[3]), .C(B[3]), .Sum(Sum[3]), .Carry(fulladder_7_carry));
  FullAdder fulladder_8 (.A(fulladder_6_carry), .B(A[7]), .C(B[7]), .Sum(Sum[7]), .Carry(CarryOut));
endmodule
