// Logisim project project1skeleton.circ as structural Verilog: 4 circuits, main circuit ALU
module Arch (
  input  [7:0] A,
  input  [7:0] B,
  input  [2:0] opcode,
  output [7:0] O
);

  ALU alu_1 (.A(A), .B(B), .opcode(opcode), .O(O));  // open: cout
endmodule

module ALU (
  input  [7:0] A,
  input  [7:0] B,
  input  [2:0] opcode,
  output [7:0] O,
  output cout
);
endmodule

module HalfAdder (
  input  A,
  input  B,
  output Sum,
  output Carry
);

  xor xor_1 (Sum, A, B);
  and and_1 (Carry, A, B);
endmodule

module FullAdder (
  input  A,
  input  B,
  input  C,
  output Sum,
  output Carry
);

  wire halfadder_1_carry, halfadder_1_sum, halfadder_2_carry;

  HalfAdder halfadder_1 (.A(B), .B(C), .Sum(halfadder_1_sum), .Carry(halfadder_1_carry));
  HalfAdder halfadder_2 (.A(A), .B(halfadder_1_sum), .Sum(Sum), .Carry(halfadder_2_carry));
  or or_1 (Carry, halfadder_2_carry, halfadder_1_carry);
endmodule
